# Fritzing sketch USBMIDItoSyncConverter-MinimumConfiguration (saved by Fritzing 1.0.3b)
breadboards: 1

parts:
  Mod1 = seeeduino-xiao
  R1 = Resistor [tolerance=±5% power=0.25W resistance=1k package=THT]
  U1 = SWITCH_SPDT [package=kps-1290]
  TRS1 = Audio Jack (TRS) 3.5mm [package="4Ucon 08780 [THT]"]

nets:
  N1: Mod1.D0, R1.Pin_0
  N2: Mod1.D1, U1.P
  N3: Mod1.GND, U1.S, TRS1.Sleeve
  N4: R1.Pin_1, TRS1.Tip

custom parts:
  seeeduino-xiao: Seeeduino XIAO processor board.
